// Digital circuit 1-bit Adder.dig as structural Verilog
module _1_bit_Adder (
  input  Input_1,
  input  Input_2,
  input  Carry_in,
  output Sum,
  output Carry_out
);

  wire and_1_out, and_2_out, xor_1_out;

  xor xor_1 (xor_1_out, Input_1, Input_2);
  and and_1 (and_1_out, Input_1, Input_2);
  xor xor_2 (Sum, xor_1_out, Carry_in);
  and and_2 (and_2_out, Carry_in, xor_1_out);
  or or_1 (Carry_out, and_2_out, and_1_out);
endmodule
