// Digital circuit 4-bit Adder.dig as structural Verilog
module _4_bit_Adder (
  input  [3:0] Input_2,
  input  Carry_in,
  input  [3:0] Input_1,
  output Carry_Out,
  output [3:0] Sum
);

  wire _1_bit_adder_1_carry_out, _1_bit_adder_2_carry_out, _1_bit_adder_3_carry_out;

  _1_bit_Adder _1_bit_adder_1 (
    .Input_1(Input_1[0]), .Sum(Sum[0]), .Input_2(Input_2[0]), .Carry_in(Carry_in),
    .Carry_out(_1_bit_adder_1_carry_out));
  _1_bit_Adder _1_bit_adder_2 (
    .Input_1(Input_1[1]), .Sum(Sum[1]), .Input_2(Input_2[1]), .Carry_in(_1_bit_adder_1_carry_out),
    .Carry_out(_1_bit_adder_2_carry_out));
  _1_bit_Adder _1_bit_adder_3 (
    .Input_1(Input_1[2]), .Sum(Sum[2]), .Input_2(Input_2[2]), .Carry_in(_1_bit_adder_2_carry_out),
    .Carry_out(_1_bit_adder_3_carry_out));
  _1_bit_Adder _1_bit_adder_4 (
    .Input_1(Input_1[3]), .Sum(Sum[3]), .Input_2(Input_2[3]), .Carry_in(_1_bit_adder_3_carry_out),
    .Carry_out(Carry_Out));
endmodule
