// Digital circuit 64-bit Adder.dig as structural Verilog
module _64_bit_Adder (
  input  [63:0] Input_2,
  input  Carry_in,
  input  [63:0] Input_1,
  output Carry_Out,
  output [63:0] Sum
);

  _16_bit_Adder _16_bit_adder_1 ();
  _16_bit_Adder _16_bit_adder_2 ();
  _16_bit_Adder _16_bit_adder_3 ();
  _16_bit_Adder _16_bit_adder_4 ();
endmodule
